// Logisim project datapath_arithmeticoverflow.circ as structural Verilog: 12 circuits, main circuit Datapath
module Datapath (
);

  wire alu_1_zero, ALUSrcA, and_1_out, CauseWrite, CLK, EPCWrite, IorD, IRWrite, MemRead, MemtoReg, MemWrite,
       or_1_out, Overflow, PCWrite, PCWriteCond, RegDst, RegWrite;
  wire [1:0] alucontrol_1_alufunct, ALUOp, ALUSrcB, IntCause, PCSource;
  wire [3:0] PC_q_2;
  wire [4:0] multiplexer_2_out;
  wire [5:0] OpCode;
  wire [25:0] InstructionReg_q;
  wire [27:0] PC_q, shiftleft26bitto28_1_out28;
  wire [31:0] A_q, alu_1_aluout, ALUOut_q, B_q, MemDataReg_q, memory_1_memdata, multiplexer_1_out,
       multiplexer_3_out, multiplexer_4_out, multiplexer_5_out, multiplexer_6_out, multiplexer_7_out,
       registerfile_1_readdata1, registerfile_1_readdata2, shiftl2_32bit_1_outshift32, signextend_1_out32,
       undriven;

  Clock u_CLK (.out(CLK));
  Register #(.width(32)) PC (.D(multiplexer_6_out), .en(or_1_out), .clk(CLK), .Q({PC_q_2, PC_q}));  // open: clr
  or or_1 (or_1_out, and_1_out, PCWrite);
  Multiplexer #(.width(32)) multiplexer_1 (.in0({PC_q_2, PC_q}), .in1(ALUOut_q), .out(multiplexer_1_out), .sel(IorD));
  and and_1 (and_1_out, alu_1_zero, PCWriteCond);
  Memory memory_1 (
    .MemRead(MemRead), .CLK(CLK), .MemAddr(multiplexer_1_out), .MemWriteData(B_q), .MemWrite(MemWrite),
    .MemData(memory_1_memdata));
  Register #(.width(32)) InstructionReg (
    .D(memory_1_memdata), .en(IRWrite), .clk(CLK), .Q({OpCode, InstructionReg_q}));  // open: clr
  Register #(.width(32)) MemDataReg (.D(memory_1_memdata), .clk(CLK), .Q(MemDataReg_q));  // open: en, clr
  Multiplexer #(.width(5)) multiplexer_2 (
    .in0(InstructionReg_q[20:16]), .in1(InstructionReg_q[15:11]), .out(multiplexer_2_out), .sel(RegDst));
  Multiplexer #(.width(32)) multiplexer_3 (.in0(ALUOut_q), .in1(MemDataReg_q), .out(multiplexer_3_out), .sel(MemtoReg));
  ControlUnit controlunit_1 (
    .Op(OpCode), .Overflow(Overflow), .CLK(CLK), .PCWriteCond(PCWriteCond), .PCWrite(PCWrite), .IorD(IorD),
    .MemRead(MemRead), .MemWrite(MemWrite), .MemtoReg(MemtoReg), .IRWrite(IRWrite), .CauseWrite(CauseWrite),
    .IntCause(IntCause), .EPCWrite(EPCWrite), .PCSource(PCSource), .ALUOp(ALUOp), .ALUSrcA(ALUSrcA),
    .ALUSrcB(ALUSrcB), .RegWrite(RegWrite), .RegDst(RegDst));
  SignExtend signextend_1 (.In16(InstructionReg_q[15:0]), .Out32(signextend_1_out32));
  RegisterFile registerfile_1 (
    .CLK(CLK), .ReadRegister2(InstructionReg_q[20:16]), .WriteEnable(RegWrite),
    .WriteRegister(multiplexer_2_out), .WriteData(multiplexer_3_out),
    .ReadRegister1(InstructionReg_q[25:21]), .ReadData1(registerfile_1_readdata1),
    .ReadData2(registerfile_1_readdata2));
  Register #(.width(32)) A (.D(registerfile_1_readdata1), .clk(CLK), .Q(A_q));  // open: en, clr
  Register #(.width(32)) B (.D(registerfile_1_readdata2), .clk(CLK), .Q(B_q));  // open: en, clr
  ShiftL2_32bit shiftl2_32bit_1 (.In32(signextend_1_out32), .OutShift32(shiftl2_32bit_1_outshift32));
  Multiplexer #(.width(32)) multiplexer_4 (.in0({PC_q_2, PC_q}), .in1(A_q), .out(multiplexer_4_out), .sel(ALUSrcA));
  Multiplexer #(.select(2), .width(32)) multiplexer_5 (
    .in0(B_q), .in1(32'h4), .in2(signextend_1_out32), .in3(shiftl2_32bit_1_outshift32),
    .out(multiplexer_5_out), .sel(ALUSrcB));
  ShiftLeft26BitTo28 shiftleft26bitto28_1 (.In26(InstructionReg_q), .Out28(shiftleft26bitto28_1_out28));
  ALU alu_1 (
    .A(multiplexer_4_out), .B(multiplexer_5_out), .ALUFunct(alucontrol_1_alufunct), .Overflow(Overflow),
    .Zero(alu_1_zero), .ALUOut(alu_1_aluout));
  ALUControl alucontrol_1 (.ALUOp(ALUOp), .Funct(InstructionReg_q[5:0]), .ALUFunct(alucontrol_1_alufunct));
  Register #(.width(32)) ALUOut (.D(alu_1_aluout), .clk(CLK), .Q(ALUOut_q));  // open: en, clr
  Multiplexer #(.select(2), .width(32)) multiplexer_6 (
    .in0(alu_1_aluout), .in1(ALUOut_q), .in2({PC_q_2, shiftleft26bitto28_1_out28}), .out(multiplexer_6_out),
    .sel(PCSource));  // open: in3
  Multiplexer #(.select(2), .width(32)) multiplexer_7 (
    .in0({32{1'b0}}), .in1(32'h1), .in2(32'hc), .in3(undriven), .out(multiplexer_7_out), .sel(IntCause));
  Register #(.width(32)) EPC (.D(alu_1_aluout), .en(EPCWrite), .clk(CLK));  // open: Q, clr
  Register #(.width(32)) Cause (.D(multiplexer_7_out), .en(CauseWrite), .clk(CLK));  // open: Q, clr
endmodule

module ALU (
  input  [31:0] A,
  input  [31:0] B,
  input  [1:0] ALUFunct,
  output Overflow,
  output Zero,
  output [31:0] ALUOut
);

  wire [0:0] comparator_1_lt;
  wire [31:0] adder_1_out, and_1_out, subtractor_1_out;

  Adder #(.width(32)) adder_1 (.a(A), .b(B), .out(adder_1_out));  // open: cin, cout
  Subtractor #(.width(32)) subtractor_1 (.a(A), .b(B), .out(subtractor_1_out));  // open: bin, bout
  assign and_1_out = A & B;  // AND_Gate and_1, 32 bits wide
  Comparator #(.width(32)) comparator_1 (.a(A), .b(B), .lt(comparator_1_lt[0]));  // open: gt, eq
  Multiplexer #(.select(2), .width(32)) multiplexer_1 (
    .in0(adder_1_out), .in1(subtractor_1_out), .in2(and_1_out), .in3({{31{1'b0}}, comparator_1_lt[0]}),
    .out(ALUOut), .sel(ALUFunct));
  Comparator #(.width(32)) comparator_2 (.a(subtractor_1_out), .b({32{1'b0}}), .eq(Zero));  // open: gt, lt
  OverflowDetect overflowdetect_1 (.SignA(A[31]), .SignB(B[31]), .SignOut(ALUOut[31]), .Overflow(Overflow));
endmodule

module ALUControl (
  input  [1:0] ALUOp,
  input  [5:0] Funct,
  output [1:0] ALUFunct
);

  wire and_1_out, and_2_out, and_3_out;

  and and_1 (and_1_out, ALUOp[1], Funct[2]);
  and and_2 (and_2_out, ALUOp[1], Funct[3]);
  and and_3 (and_3_out, ALUOp[1], Funct[1]);
  or or_1 (ALUFunct[1], and_1_out, and_2_out);
  or or_2 (ALUFunct[0], and_3_out, ALUOp[0]);
endmodule

module RegisterFile (
  input  WriteEnable,
  input  [4:0] WriteRegister,
  input  [31:0] WriteData,
  input  [4:0] ReadRegister1,
  input  [4:0] ReadRegister2,
  input  CLK,
  output [31:0] ReadData1,
  output [31:0] ReadData2
);

  wire and_1_out, and_2_out, and_3_out, and_4_out, and_5_out, and_6_out, and_7_out, and_8_out, and_9_out,
       and_10_out, and_11_out, and_12_out, and_13_out, and_14_out, and_15_out, and_16_out, and_17_out,
       and_18_out, and_19_out, and_20_out, and_21_out, and_22_out, and_23_out, and_24_out, and_25_out,
       and_26_out, and_27_out, and_28_out, and_29_out, and_30_out, and_31_out, and_32_out, decoder_1_out0,
       decoder_1_out1, decoder_1_out2, decoder_1_out3, decoder_1_out4, decoder_1_out5, decoder_1_out6,
       decoder_1_out7, decoder_1_out8, decoder_1_out9, decoder_1_out10, decoder_1_out11, decoder_1_out12,
       decoder_1_out13, decoder_1_out14, decoder_1_out15, decoder_1_out16, decoder_1_out17, decoder_1_out18,
       decoder_1_out19, decoder_1_out20, decoder_1_out21, decoder_1_out22, decoder_1_out23, decoder_1_out24,
       decoder_1_out25, decoder_1_out26, decoder_1_out27, decoder_1_out28, decoder_1_out29, decoder_1_out30,
       decoder_1_out31;
  wire [31:0] r0_q, r1_q, r2_q, r3_q, r4_q, r5_q, r6_q, r7_q, r8_q, r9_q, r10_q, r11_q, r12_q, r13_q, r14_q,
       r15_q, r16_q, r17_q, r18_q, r19_q, r20_q, r21_q, r22_q, r23_q, r24_q, r25_q, r26_q, r27_q, r28_q,
       r29_q, r30_q, r31_q;

  Decoder #(.select(5)) decoder_1 (
    .out0(decoder_1_out0), .out1(decoder_1_out1), .out2(decoder_1_out2), .out3(decoder_1_out3),
    .out4(decoder_1_out4), .out5(decoder_1_out5), .out6(decoder_1_out6), .out7(decoder_1_out7),
    .out8(decoder_1_out8), .out9(decoder_1_out9), .out10(decoder_1_out10), .out11(decoder_1_out11),
    .out12(decoder_1_out12), .out13(decoder_1_out13), .out14(decoder_1_out14), .out15(decoder_1_out15),
    .out16(decoder_1_out16), .out17(decoder_1_out17), .out18(decoder_1_out18), .out19(decoder_1_out19),
    .out20(decoder_1_out20), .out21(decoder_1_out21), .out22(decoder_1_out22), .out23(decoder_1_out23),
    .out24(decoder_1_out24), .out25(decoder_1_out25), .out26(decoder_1_out26), .out27(decoder_1_out27),
    .out28(decoder_1_out28), .out29(decoder_1_out29), .out30(decoder_1_out30), .out31(decoder_1_out31),
    .sel(WriteRegister));  // open: en
  and and_1 (and_1_out, decoder_1_out0, WriteEnable);
  and and_2 (and_2_out, decoder_1_out1, WriteEnable);
  and and_3 (and_3_out, decoder_1_out2, WriteEnable);
  and and_4 (and_4_out, decoder_1_out3, WriteEnable);
  and and_5 (and_5_out, decoder_1_out4, WriteEnable);
  and and_6 (and_6_out, decoder_1_out5, WriteEnable);
  and and_7 (and_7_out, decoder_1_out6, WriteEnable);
  and and_8 (and_8_out, decoder_1_out7, WriteEnable);
  and and_9 (and_9_out, decoder_1_out8, WriteEnable);
  and and_10 (and_10_out, decoder_1_out9, WriteEnable);
  and and_11 (and_11_out, decoder_1_out10, WriteEnable);
  and and_12 (and_12_out, decoder_1_out11, WriteEnable);
  and and_13 (and_13_out, decoder_1_out12, WriteEnable);
  and and_14 (and_14_out, decoder_1_out13, WriteEnable);
  and and_15 (and_15_out, decoder_1_out14, WriteEnable);
  and and_16 (and_16_out, decoder_1_out15, WriteEnable);
  and and_17 (and_17_out, decoder_1_out16, WriteEnable);
  and and_18 (and_18_out, decoder_1_out17, WriteEnable);
  and and_19 (and_19_out, decoder_1_out18, WriteEnable);
  and and_20 (and_20_out, decoder_1_out19, WriteEnable);
  and and_21 (and_21_out, decoder_1_out20, WriteEnable);
  and and_22 (and_22_out, decoder_1_out21, WriteEnable);
  and and_23 (and_23_out, decoder_1_out22, WriteEnable);
  and and_24 (and_24_out, decoder_1_out23, WriteEnable);
  and and_25 (and_25_out, decoder_1_out24, WriteEnable);
  and and_26 (and_26_out, decoder_1_out25, WriteEnable);
  and and_27 (and_27_out, decoder_1_out26, WriteEnable);
  and and_28 (and_28_out, decoder_1_out27, WriteEnable);
  and and_29 (and_29_out, decoder_1_out28, WriteEnable);
  and and_30 (and_30_out, decoder_1_out29, WriteEnable);
  and and_31 (and_31_out, decoder_1_out30, WriteEnable);
  and and_32 (and_32_out, decoder_1_out31, WriteEnable);
  Register #(.width(32)) r0 (.D(WriteData), .en(and_1_out), .clk(CLK), .Q(r0_q));  // open: clr
  Register #(.width(32)) r1 (.D(WriteData), .en(and_2_out), .clk(CLK), .Q(r1_q));  // open: clr
  Register #(.width(32)) r2 (.D(WriteData), .en(and_3_out), .clk(CLK), .Q(r2_q));  // open: clr
  Register #(.width(32)) r3 (.D(WriteData), .en(and_4_out), .clk(CLK), .Q(r3_q));  // open: clr
  Register #(.width(32)) r4 (.D(WriteData), .en(and_5_out), .clk(CLK), .Q(r4_q));  // open: clr
  Register #(.width(32)) r5 (.D(WriteData), .en(and_6_out), .clk(CLK), .Q(r5_q));  // open: clr
  Register #(.width(32)) r6 (.D(WriteData), .en(and_7_out), .clk(CLK), .Q(r6_q));  // open: clr
  Register #(.width(32)) r7 (.D(WriteData), .en(and_8_out), .clk(CLK), .Q(r7_q));  // open: clr
  Register #(.width(32)) r8 (.D(WriteData), .en(and_9_out), .clk(CLK), .Q(r8_q));  // open: clr
  Register #(.width(32)) r9 (.D(WriteData), .en(and_10_out), .clk(CLK), .Q(r9_q));  // open: clr
  Register #(.width(32)) r10 (.D(WriteData), .en(and_11_out), .clk(CLK), .Q(r10_q));  // open: clr
  Register #(.width(32)) r11 (.D(WriteData), .en(and_12_out), .clk(CLK), .Q(r11_q));  // open: clr
  Register #(.width(32)) r12 (.D(WriteData), .en(and_13_out), .clk(CLK), .Q(r12_q));  // open: clr
  Register #(.width(32)) r13 (.D(WriteData), .en(and_14_out), .clk(CLK), .Q(r13_q));  // open: clr
  Register #(.width(32)) r14 (.D(WriteData), .en(and_15_out), .clk(CLK), .Q(r14_q));  // open: clr
  Register #(.width(32)) r15 (.D(WriteData), .en(and_16_out), .clk(CLK), .Q(r15_q));  // open: clr
  Register #(.width(32)) r16 (.D(WriteData), .en(and_17_out), .clk(CLK), .Q(r16_q));  // open: clr
  Register #(.width(32)) r17 (.D(WriteData), .en(and_18_out), .clk(CLK), .Q(r17_q));  // open: clr
  Register #(.width(32)) r18 (.D(WriteData), .en(and_19_out), .clk(CLK), .Q(r18_q));  // open: clr
  Register #(.width(32)) r19 (.D(WriteData), .en(and_20_out), .clk(CLK), .Q(r19_q));  // open: clr
  Register #(.width(32)) r20 (.D(WriteData), .en(and_21_out), .clk(CLK), .Q(r20_q));  // open: clr
  Register #(.width(32)) r21 (.D(WriteData), .en(and_22_out), .clk(CLK), .Q(r21_q));  // open: clr
  Register #(.width(32)) r22 (.D(WriteData), .en(and_23_out), .clk(CLK), .Q(r22_q));  // open: clr
  Register #(.width(32)) r23 (.D(WriteData), .en(and_24_out), .clk(CLK), .Q(r23_q));  // open: clr
  Register #(.width(32)) r24 (.D(WriteData), .en(and_25_out), .clk(CLK), .Q(r24_q));  // open: clr
  Register #(.width(32)) r25 (.D(WriteData), .en(and_26_out), .clk(CLK), .Q(r25_q));  // open: clr
  Register #(.width(32)) r26 (.D(WriteData), .en(and_27_out), .clk(CLK), .Q(r26_q));  // open: clr
  Register #(.width(32)) r27 (.D(WriteData), .en(and_28_out), .clk(CLK), .Q(r27_q));  // open: clr
  Register #(.width(32)) r28 (.D(WriteData), .en(and_29_out), .clk(CLK), .Q(r28_q));  // open: clr
  Register #(.width(32)) r29 (.D(WriteData), .en(and_30_out), .clk(CLK), .Q(r29_q));  // open: clr
  Register #(.width(32)) r30 (.D(WriteData), .en(and_31_out), .clk(CLK), .Q(r30_q));  // open: clr
  Register #(.width(32)) r31 (.D(WriteData), .en(and_32_out), .clk(CLK), .Q(r31_q));  // open: clr
  Multiplexer #(.select(5), .width(32)) multiplexer_1 (
    .in0(r0_q), .in1(r1_q), .in2(r2_q), .in3(r3_q), .in4(r4_q), .in5(r5_q), .in6(r6_q), .in7(r7_q),
    .in8(r8_q), .in9(r9_q), .in10(r10_q), .in11(r11_q), .in12(r12_q), .in13(r13_q), .in14(r14_q),
    .in15(r15_q), .in16(r16_q), .in17(r17_q), .in18(r18_q), .in19(r19_q), .in20(r20_q), .in21(r21_q),
    .in22(r22_q), .in23(r23_q), .in24(r24_q), .in25(r25_q), .in26(r26_q), .in27(r27_q), .in28(r28_q),
    .in29(r29_q), .in30(r30_q), .in31(r31_q), .out(ReadData1), .sel(ReadRegister1));
  Multiplexer #(.select(5), .width(32)) multiplexer_2 (
    .in0(r0_q), .in1(r1_q), .in2(r2_q), .in3(r3_q), .in4(r4_q), .in5(r5_q), .in6(r6_q), .in7(r7_q),
    .in8(r8_q), .in9(r9_q), .in10(r10_q), .in11(r11_q), .in12(r12_q), .in13(r13_q), .in14(r14_q),
    .in15(r15_q), .in16(r16_q), .in17(r17_q), .in18(r18_q), .in19(r19_q), .in20(r20_q), .in21(r21_q),
    .in22(r22_q), .in23(r23_q), .in24(r24_q), .in25(r25_q), .in26(r26_q), .in27(r27_q), .in28(r28_q),
    .in29(r29_q), .in30(r30_q), .in31(r31_q), .out(ReadData2), .sel(ReadRegister2));
endmodule

module Memory (
  input  [31:0] MemAddr,
  input  MemWrite,
  input  [31:0] MemWriteData,
  input  MemRead,
  input  CLK,
  output [31:0] MemData
);

  wire [31:0] ram_1_dout;

  RAM #(.addrWidth(24), .dataWidth(32), .enables("line"), .\type ("nonvolatile")) ram_1 (
    .addr(MemAddr[25:2]), .we(MemWrite), .clk(CLK), .din(MemWriteData), .dout(ram_1_dout));
  Register #(.trigger("high"), .width(32)) register_1 (
    .D(ram_1_dout), .en(MemRead), .clk(MemRead), .Q(MemData));  // open: clr
endmodule

module SignExtend (
  input  [15:0] In16,
  output [31:0] Out32
);


  assign Out32 = {{17{In16[15]}}, In16[14:0]};
endmodule

module ShiftL2_32bit (
  input  [31:0] In32,
  output [31:0] OutShift32
);

  Shifter #(.width(32)) shifter_1 (.in(In32), .\dist (5'b00010), .out(OutShift32));
endmodule

module ShiftLeft26BitTo28 (
  input  [25:0] In26,
  output [27:0] Out28
);


  assign Out28 = {In26, 2'b00};
endmodule

module ControlUnit (
  input  [5:0] Op,
  input  Overflow,
  input  CLK,
  output PCWriteCond,
  output PCWrite,
  output IorD,
  output MemRead,
  output MemWrite,
  output MemtoReg,
  output IRWrite,
  output CauseWrite,
  output [1:0] IntCause,
  output EPCWrite,
  output [1:0] PCSource,
  output [1:0] ALUOp,
  output ALUSrcA,
  output [1:0] ALUSrcB,
  output RegWrite,
  output RegDst
);

  wire [3:0] CurrentState_q, nextstatecontrolunit_1_nextstate;

  NextStateControlUnit nextstatecontrolunit_1 (
    .CurrentState(CurrentState_q), .Op(Op), .Overflow(Overflow), .NextState(nextstatecontrolunit_1_nextstate));
  Register #(.width(4)) CurrentState (
    .D(nextstatecontrolunit_1_nextstate), .en(1'b1), .clk(CLK), .Q(CurrentState_q));  // open: clr
  OutputControlUnit outputcontrolunit_1 (
    .CurrentState(CurrentState_q), .PCWriteCond(PCWriteCond), .PCWrite(PCWrite), .IorD(IorD),
    .MemRead(MemRead), .MemWrite(MemWrite), .MemtoReg(MemtoReg), .IRWrite(IRWrite), .CauseWrite(CauseWrite),
    .IntCause(IntCause), .EPCWrite(EPCWrite), .PCSource(PCSource), .ALUOp(ALUOp), .ALUSrcA(ALUSrcA),
    .ALUSrcB(ALUSrcB), .RegWrite(RegWrite), .RegDst(RegDst));
endmodule

module OverflowDetect (
  input  SignA,
  input  SignB,
  input  SignOut,
  output Overflow
);

  wire and_1_out, and_2_out, not_1_out, not_2_out, not_3_out;

  not not_1 (not_1_out, SignA);
  not not_2 (not_2_out, SignB);
  not not_3 (not_3_out, SignOut);
  and and_1 (and_1_out, not_1_out, not_2_out, SignOut);
  and and_2 (and_2_out, SignA, SignB, not_3_out);
  or or_1 (Overflow, and_1_out, and_2_out);
endmodule

module NextStateControlUnit (
  input  [3:0] CurrentState,
  input  [5:0] Op,
  input  Overflow,
  output [3:0] NextState
);

  wire not_1_out, not_2_out, not_3_out, not_4_out, not_5_out, not_6_out, not_7_out, not_8_out, not_9_out,
       not_10_out, not_11_out, or_1_out, or_2_out, or_3_out, or_4_out, or_5_out, or_6_out, or_7_out,
       or_8_out, or_9_out, or_10_out, or_11_out, or_12_out, or_13_out, or_14_out, or_15_out, or_16_out,
       or_17_out, or_18_out, or_19_out, or_20_out, or_21_out, or_22_out, or_23_out, or_24_out, or_25_out,
       or_26_out, or_27_out, or_28_out, or_29_out, or_30_out, or_31_out, or_32_out, or_33_out, or_34_out,
       or_35_out, or_36_out, or_37_out, or_38_out, or_39_out, or_40_out, or_41_out, or_42_out, or_43_out,
       or_44_out, or_45_out, or_46_out, or_47_out, or_48_out, or_49_out, or_50_out, or_51_out;

  not not_1 (not_1_out, CurrentState[3]);
  not not_2 (not_2_out, CurrentState[2]);
  not not_3 (not_3_out, CurrentState[1]);
  not not_4 (not_4_out, CurrentState[0]);
  not not_5 (not_5_out, Op[5]);
  not not_6 (not_6_out, Op[4]);
  not not_7 (not_7_out, Op[3]);
  not not_8 (not_8_out, Op[2]);
  not not_9 (not_9_out, Op[1]);
  not not_10 (not_10_out, Op[0]);
  not not_11 (not_11_out, Overflow);
  or or_1 (or_1_out, CurrentState[2], not_3_out);
  or or_2 (or_2_out, not_2_out, CurrentState[1]);
  or or_3 (or_3_out, not_1_out, CurrentState[0]);
  or or_4 (or_4_out, Op[5], Op[4], Op[3], Op[2], Op[1], Op[0], Overflow);
  or or_5 (or_5_out, CurrentState[1], Op[5], Op[4], Op[3], Op[2], Op[1], Op[0]);
  or or_6 (or_6_out, CurrentState[0], Overflow);
  or or_7 (or_7_out, CurrentState[1], CurrentState[0]);
  or or_8 (or_8_out, not_5_out, Op[4], Op[2], not_9_out, not_10_out, Overflow);
  or or_9 (or_9_out, CurrentState[2], not_5_out, Op[4], Op[2], not_9_out, not_10_out);
  or or_10 (or_10_out, not_2_out, Overflow);
  or or_11 (or_11_out, not_1_out, Overflow);
  or or_12 (or_12_out, not_1_out, CurrentState[1]);
  or or_13 (or_13_out, CurrentState[1], not_10_out);
  or or_14 (or_14_out, CurrentState[1], not_9_out);
  or or_15 (or_15_out, CurrentState[1], not_8_out);
  or or_16 (or_16_out, CurrentState[1], not_7_out);
  or or_17 (or_17_out, CurrentState[1], not_6_out);
  or or_18 (or_18_out, CurrentState[1], not_5_out);
  or or_19 (or_19_out, CurrentState[2], CurrentState[0], Op[3]);
  or or_20 (or_20_out, CurrentState[3], not_2_out, not_11_out);
  or or_21 (or_21_out, not_2_out, not_4_out);
  or or_22 (or_22_out, not_1_out, CurrentState[2]);
  or or_23 (or_23_out, CurrentState[1], CurrentState[0]);
  or or_24 (or_24_out, CurrentState[1], CurrentState[0]);
  or or_25 (or_25_out, CurrentState[2], not_3_out, not_4_out);
  or or_26 (or_26_out, not_2_out, CurrentState[1]);
  or or_27 (or_27_out, not_1_out, CurrentState[2]);
  or or_28 (or_28_out, not_4_out, Op[5], Op[4], Op[3], Op[2], not_9_out, Op[0], Overflow);
  or or_29 (or_29_out, CurrentState[2], not_4_out, Op[5], Op[4], Op[3], Op[2], not_9_out, Op[0]);
  or or_30 (or_30_out, not_4_out, Op[5], Op[4], Op[3], not_8_out, Op[1], Op[0], Overflow);
  or or_31 (or_31_out, CurrentState[2], not_4_out, Op[5], Op[4], Op[3], not_8_out, Op[1], Op[0]);
  or or_32 (or_32_out, CurrentState[2], CurrentState[0], not_7_out);
  or or_33 (or_33_out, not_2_out, not_4_out, Overflow);
  or or_34 (or_34_out, CurrentState[2], not_3_out, not_4_out);
  or or_35 (or_35_out, not_2_out, CurrentState[1]);
  or or_36 (or_36_out, not_1_out, CurrentState[0]);
  or or_37 (or_37_out, not_4_out, Op[1], Overflow);
  or or_38 (or_38_out, CurrentState[1], not_4_out, Op[1]);
  or or_39 (or_39_out, not_4_out, not_10_out, Overflow);
  or or_40 (or_40_out, CurrentState[1], not_4_out, not_10_out);
  or or_41 (or_41_out, not_4_out, not_8_out, Overflow);
  or or_42 (or_42_out, CurrentState[2], not_4_out, not_8_out);
  or or_43 (or_43_out, not_4_out, not_7_out, Overflow);
  or or_44 (or_44_out, CurrentState[1], not_4_out, not_7_out);
  or or_45 (or_45_out, not_4_out, not_6_out, Overflow);
  or or_46 (or_46_out, CurrentState[1], not_4_out, not_6_out);
  or or_47 (or_47_out, not_4_out, not_5_out, Overflow);
  or or_48 (or_48_out, CurrentState[1], not_4_out, not_5_out);
  or or_49 (or_49_out, not_3_out, not_4_out, Overflow);
  or or_50 (or_50_out, not_1_out, Overflow);
  or or_51 (or_51_out, not_1_out, CurrentState[1]);
  and and_1 (NextState[2], or_13_out, or_14_out, or_15_out, or_16_out, or_17_out, or_18_out, or_19_out, or_20_out, or_21_out, or_22_out, or_23_out);
  and and_2 (NextState[1], or_24_out, or_25_out, or_26_out, or_27_out, or_28_out, or_29_out, or_30_out, or_31_out, or_32_out, or_33_out);
  and and_3 (NextState[3], or_1_out, or_2_out, or_3_out, or_4_out, or_5_out, or_6_out, or_7_out, or_8_out, or_9_out, or_10_out, or_11_out, or_12_out);
  and and_4 (NextState[0], or_34_out, or_35_out, or_36_out, or_37_out, or_38_out, or_39_out, or_40_out, or_41_out, or_42_out, or_43_out, or_44_out, or_45_out, or_46_out, or_47_out, or_48_out, or_49_out, or_50_out, or_51_out);
endmodule

module OutputControlUnit (
  input  [3:0] CurrentState,
  output PCWriteCond,
  output PCWrite,
  output IorD,
  output MemRead,
  output MemWrite,
  output MemtoReg,
  output IRWrite,
  output CauseWrite,
  output [1:0] IntCause,
  output EPCWrite,
  output [1:0] PCSource,
  output [1:0] ALUOp,
  output ALUSrcA,
  output [1:0] ALUSrcB,
  output RegWrite,
  output RegDst
);

  wire and_2_out, and_3_out, and_4_out, and_5_out, and_6_out, and_7_out, and_8_out, and_15_out, and_16_out,
       and_17_out, and_18_out, and_20_out, and_21_out, and_22_out, and_23_out, and_24_out, and_25_out,
       and_26_out, and_27_out, and_28_out, and_29_out, not_1_out, not_2_out, not_3_out, not_4_out;

  not not_1 (not_1_out, CurrentState[3]);
  not not_2 (not_2_out, CurrentState[2]);
  not not_3 (not_3_out, CurrentState[1]);
  not not_4 (not_4_out, CurrentState[0]);
  and and_1 (PCWriteCond, CurrentState[3], not_3_out, not_4_out);
  and and_2 (and_2_out, not_1_out, not_2_out, not_3_out, not_4_out);
  and and_3 (and_3_out, CurrentState[3], not_2_out, CurrentState[0]);
  and and_4 (and_4_out, CurrentState[3], not_3_out, CurrentState[0]);
  and and_5 (and_5_out, not_1_out, not_2_out, CurrentState[1], CurrentState[0]);
  and and_6 (and_6_out, CurrentState[2], not_3_out, CurrentState[0]);
  and and_7 (and_7_out, not_1_out, not_2_out, not_3_out, not_4_out);
  and and_8 (and_8_out, not_1_out, not_2_out, CurrentState[1], CurrentState[0]);
  and and_9 (MemWrite, CurrentState[2], not_3_out, CurrentState[0]);
  and and_10 (MemtoReg, CurrentState[2], not_3_out, not_4_out);
  and and_11 (IRWrite, not_1_out, not_2_out, not_3_out, not_4_out);
  and and_12 (CauseWrite, CurrentState[3], not_2_out, CurrentState[1], CurrentState[0]);
  and and_13 (IntCause[1], not_2_out, CurrentState[1], CurrentState[0]);
  and and_14 (EPCWrite, CurrentState[3], not_2_out, CurrentState[1], CurrentState[0]);
  and and_15 (and_15_out, CurrentState[3], not_2_out, CurrentState[0]);
  and and_16 (and_16_out, CurrentState[3], not_3_out, CurrentState[0]);
  and and_17 (and_17_out, CurrentState[3], not_3_out, not_4_out);
  and and_18 (and_18_out, CurrentState[3], not_2_out, CurrentState[1], CurrentState[0]);
  and and_19 (ALUOp[1], CurrentState[2], CurrentState[1], not_4_out);
  and and_20 (and_20_out, CurrentState[3], not_3_out, not_4_out);
  and and_21 (and_21_out, CurrentState[3], not_2_out, CurrentState[1], CurrentState[0]);
  and and_22 (and_22_out, not_1_out, CurrentState[1], not_4_out);
  and and_23 (and_23_out, CurrentState[3], not_3_out, not_4_out);
  and and_24 (and_24_out, not_1_out, not_2_out, not_3_out, CurrentState[0]);
  and and_25 (and_25_out, not_1_out, not_2_out, CurrentState[1], not_4_out);
  and and_26 (and_26_out, not_1_out, not_2_out, not_3_out);
  and and_27 (and_27_out, CurrentState[3], not_2_out, CurrentState[1], CurrentState[0]);
  and and_28 (and_28_out, CurrentState[2], not_3_out, not_4_out);
  and and_29 (and_29_out, CurrentState[2], CurrentState[1], CurrentState[0]);
  and and_30 (RegDst, CurrentState[2], CurrentState[1], CurrentState[0]);
  or or_1 (PCWrite, and_2_out, and_3_out, and_4_out);
  or or_2 (IorD, and_5_out, and_6_out);
  or or_3 (MemRead, and_7_out, and_8_out);
  or or_4 (PCSource[1], and_15_out, and_16_out);
  or or_5 (PCSource[0], and_17_out, and_18_out);
  or or_6 (ALUOp[0], and_20_out, and_21_out);
  or or_7 (ALUSrcA, and_22_out, and_23_out);
  or or_8 (ALUSrcB[1], and_24_out, and_25_out);
  or or_9 (ALUSrcB[0], and_26_out, and_27_out);
  or or_10 (RegWrite, and_28_out, and_29_out);

  assign IntCause[0] = 1'b0;
endmodule
